// Logisim project CSE332-16bits-ISA-Project.circ as structural Verilog
module _16_Bits_Register (
  input  [15:0] Write_Data,
  input  [3:0] Read_Register_1___RS,
  input  [3:0] Read_Register_2__RT,
  input  [3:0] Write_Register_RD,
  input  Register_Write,
  input  CLK,
  output [15:0] Read_Data_1,
  output [15:0] Read_Data_2
);

  wire and_1_out, and_2_out, and_3_out, and_4_out, and_5_out, and_6_out, and_7_out, and_8_out, and_9_out,
       and_10_out, and_11_out, and_12_out, and_13_out, and_14_out, and_15_out, and_16_out, decoder_1_out0,
       decoder_1_out1, decoder_1_out2, decoder_1_out3, decoder_1_out4, decoder_1_out5, decoder_1_out6,
       decoder_1_out7, decoder_1_out8, decoder_1_out9, decoder_1_out10, decoder_1_out11, decoder_1_out12,
       decoder_1_out13, decoder_1_out14, decoder_1_out15;
  wire [15:0] R0_q, R1_q, R2_q, R3_q, R4_q, R5_q, R6_q, R7_q, R8_q, R9_q, R10_q, R11_q, R12_q, R13_q, R14_q,
       R15_q, undriven;

  Decoder #(.select(4), .enable("false")) decoder_1 (
    .out0(decoder_1_out0), .out1(decoder_1_out1), .out2(decoder_1_out2), .out3(decoder_1_out3),
    .out4(decoder_1_out4), .out5(decoder_1_out5), .out6(decoder_1_out6), .out7(decoder_1_out7),
    .out8(decoder_1_out8), .out9(decoder_1_out9), .out10(decoder_1_out10), .out11(decoder_1_out11),
    .out12(decoder_1_out12), .out13(decoder_1_out13), .out14(decoder_1_out14), .out15(decoder_1_out15),
    .sel(Write_Register_RD));
  and and_1 (and_1_out, decoder_1_out0, Register_Write);
  and and_2 (and_2_out, decoder_1_out1, Register_Write);
  and and_3 (and_3_out, decoder_1_out2, Register_Write);
  and and_4 (and_4_out, decoder_1_out3, Register_Write);
  and and_5 (and_5_out, Register_Write, decoder_1_out4);
  and and_6 (and_6_out, Register_Write, decoder_1_out5);
  and and_7 (and_7_out, Register_Write, decoder_1_out6);
  and and_8 (and_8_out, Register_Write, decoder_1_out7);
  and and_9 (and_9_out, Register_Write, decoder_1_out8);
  and and_10 (and_10_out, Register_Write, decoder_1_out9);
  and and_11 (and_11_out, Register_Write, decoder_1_out10);
  and and_12 (and_12_out, Register_Write, decoder_1_out11);
  and and_13 (and_13_out, Register_Write, decoder_1_out12);
  and and_14 (and_14_out, Register_Write, decoder_1_out13);
  and and_15 (and_15_out, Register_Write, decoder_1_out14);
  and and_16 (and_16_out, Register_Write, decoder_1_out15);
  Register #(.width(16)) R0 (.D(Write_Data), .en(and_1_out), .Q(R0_q), .clk(CLK));  // open: clr
  Register #(.width(16)) R1 (.D(Write_Data), .en(and_2_out), .Q(R1_q), .clk(CLK));  // open: clr
  Register #(.width(16)) R2 (.D(Write_Data), .en(and_3_out), .Q(R2_q), .clk(CLK));  // open: clr
  Register #(.width(16)) R3 (.D(Write_Data), .en(and_4_out), .Q(R3_q), .clk(CLK));  // open: clr
  Register #(.width(16)) R4 (.D(Write_Data), .en(and_5_out), .Q(R4_q), .clk(CLK));  // open: clr
  Register #(.width(16)) R5 (.D(Write_Data), .en(and_6_out), .Q(R5_q), .clk(CLK));  // open: clr
  Register #(.width(16)) R6 (.D(Write_Data), .en(and_7_out), .Q(R6_q), .clk(CLK));  // open: clr
  Register #(.width(16)) R7 (.D(Write_Data), .en(and_8_out), .Q(R7_q), .clk(CLK));  // open: clr
  Register #(.width(16)) R8 (.D(undriven), .en(and_9_out), .Q(R8_q), .clk(CLK));  // open: clr
  Register #(.width(16)) R9 (.D(undriven), .en(and_10_out), .Q(R9_q), .clk(CLK));  // open: clr
  Register #(.width(16)) R10 (.D(undriven), .en(and_11_out), .Q(R10_q), .clk(CLK));  // open: clr
  Register #(.width(16)) R11 (.D(undriven), .en(and_12_out), .Q(R11_q), .clk(CLK));  // open: clr
  Register #(.width(16)) R12 (.D(undriven), .en(and_13_out), .Q(R12_q), .clk(CLK));  // open: clr
  Register #(.width(16)) R13 (.D(undriven), .en(and_14_out), .Q(R13_q), .clk(CLK));  // open: clr
  Register #(.width(16)) R14 (.D(undriven), .en(and_15_out), .Q(R14_q), .clk(CLK));  // open: clr
  Register #(.width(16)) R15 (.D(undriven), .en(and_16_out), .Q(R15_q), .clk(CLK));  // open: clr
  Multiplexer #(.select(4), .width(16), .enable("false")) multiplexer_1 (
    .in0(R0_q), .in1(R1_q), .in2(R2_q), .in3(R3_q), .in4(R4_q), .in5(R5_q), .in6(R6_q), .in7(R7_q),
    .in8(R8_q), .in9(R9_q), .in10(R10_q), .in11(R11_q), .in12(R12_q), .in13(R13_q), .in14(R14_q),
    .in15(R15_q), .out(Read_Data_1), .sel(Read_Register_1___RS));
  Multiplexer #(.select(4), .width(16), .enable("false")) multiplexer_2 (
    .in0(R0_q), .in1(R1_q), .in2(R2_q), .in3(R3_q), .in4(R4_q), .in5(R5_q), .in6(R6_q), .in7(R7_q),
    .in8(R8_q), .in9(R9_q), .in10(R10_q), .in11(R11_q), .in12(R12_q), .in13(R13_q), .in14(R14_q),
    .in15(R15_q), .out(Read_Data_2), .sel(Read_Register_2__RT));
endmodule

module _16_Bits_ALU (
  input  [15:0] A,
  input  C_in,
  input  [15:0] B,
  input  [1:0] ALU_op,
  input  B_inv,
  output [15:0] Result,
  output C_out
);

  wire [15:0] adder_1_out, adder_2_out, and_1_out, multiplexer_1_out, not_1_out, or_1_out;

  Multiplexer #(.width(16), .enable("false")) multiplexer_1 (
    .in0(B), .in1(not_1_out), .out(multiplexer_1_out), .sel(B_inv));
  assign not_1_out = ~B;  // NOT_Gate not_1, 16 bits wide
  Adder #(.width(16)) adder_1 (.a(A), .b(multiplexer_1_out), .out(adder_1_out));  // open: cin, cout
  Adder #(.width(16)) adder_2 (.a(A), .b(multiplexer_1_out), .out(adder_2_out), .cin(C_in), .cout(C_out));
  assign and_1_out = A & multiplexer_1_out;  // AND_Gate and_1, 16 bits wide
  assign or_1_out = A | multiplexer_1_out;  // OR_Gate or_1, 16 bits wide
  Multiplexer #(.select(2), .width(16), .enable("false")) multiplexer_2 (
    .in0(adder_1_out), .in1(adder_2_out), .in2(and_1_out), .in3(or_1_out), .out(Result), .sel(ALU_op));
endmodule

module _4_bit_Control_Unit (
  input  [3:0] Opcode,
  output Reg_WriteEn,
  output B_inv,
  output C_in,
  output [1:0] ALU_op
);

  wire add0000_out, AND0010_out, OR0011_out;

  and add0000 (add0000_out, ~Opcode[3], ~Opcode[2], ~Opcode[1], ~Opcode[0]);  // AND_Gate
  and sub0001 (B_inv, ~Opcode[3], ~Opcode[2], ~Opcode[1], Opcode[0]);  // AND_Gate
  and AND0010 (AND0010_out, ~Opcode[3], ~Opcode[2], Opcode[1], ~Opcode[0]);  // AND_Gate
  and OR0011 (OR0011_out, ~Opcode[3], ~Opcode[2], Opcode[1], Opcode[0]);  // AND_Gate
  or or_1 (Reg_WriteEn, add0000_out, B_inv, AND0010_out, OR0011_out);
  or or_2 (ALU_op[0], B_inv, OR0011_out);
  or or_3 (ALU_op[1], AND0010_out, OR0011_out);

  assign C_in = B_inv;
endmodule

module DATAPATH (
  input  Clr,
  output [3:0] Opcode,
  output [3:0] RD,
  output [3:0] RS,
  output [3:0] RT,
  output out_6,
  output [15:0] out_7
);

  wire clock_1_out, n4_bit_control_unit_1_b_inv, n4_bit_control_unit_1_c_in,
       n4_bit_control_unit_1_reg_writeen;
  wire [1:0] adder_1_out, n4_bit_control_unit_1_alu_op, register_1_q;
  wire [15:0] bit_extender_1_out, n16_bits_alu_1_result, n16_bits_register_1_read_data_1,
       n16_bits_register_1_read_data_2;

  Clock clock_1 (.out(clock_1_out));
  Register #(.width(2)) register_1 (.D(adder_1_out), .Q(register_1_q), .clk(clock_1_out));  // open: en, clr
  Adder #(.width(2)) adder_1 (.a(2'b01), .b(register_1_q), .out(adder_1_out), .cin(1'b0));  // open: cout
  _4_bit_Control_Unit u_4_bit_control_unit_1 (
    .Opcode(Opcode), .Reg_WriteEn(n4_bit_control_unit_1_reg_writeen), .B_inv(n4_bit_control_unit_1_b_inv),
    .C_in(n4_bit_control_unit_1_c_in), .ALU_op(n4_bit_control_unit_1_alu_op));
  ROM #(.addrWidth(2), .dataWidth(16)) rom_1 (.addr(register_1_q), .data({Opcode, RD, RS, RT}));  // open: sel
  _16_Bits_Register u_16_bits_register_1 (
    .Write_Data(n16_bits_alu_1_result), .Read_Data_1(n16_bits_register_1_read_data_1),
    .Read_Data_2(n16_bits_register_1_read_data_2), .Write_Register_RD(RD),
    .Register_Write(n4_bit_control_unit_1_reg_writeen), .CLK(clock_1_out), .Read_Register_1___RS(RS),
    .Read_Register_2__RT(RT));
  assign bit_extender_1_out = {{12{1'b0}}, RD};  // Bit_Extender bit_extender_1
  _16_Bits_ALU u_16_bits_alu_1 (
    .A(n16_bits_register_1_read_data_1), .B(n16_bits_register_1_read_data_2),
    .ALU_op(n4_bit_control_unit_1_alu_op), .B_inv(n4_bit_control_unit_1_b_inv),
    .Result(n16_bits_alu_1_result), .C_in(n4_bit_control_unit_1_c_in), .C_out(out_6));
  RAM #(.addrWidth(16), .dataWidth(16), .bus("separate")) ram_1 (
    .addr(bit_extender_1_out), .din(n16_bits_alu_1_result), .data(out_7), .clk(clock_1_out), .clr(Clr));  // open: str, sel, ld

  // Notes on the sheet:
  //   ROM (Inst. Memory)
  //   contents of rom_1 (hex, n*v repeats v):
  //   512 1312 2412 3612
  //                             RAM(Data Memory)
endmodule
